# Fritzing sketch light-cube-wiring (saved by Fritzing 0.9.10b)
breadboards: 1

parts:
  M2 = Arduino Nano 33 IOT-tht
  IC2 = IC, DIP package, 14 pins [chip_label=IC]
  Part3 = NeoPixel NeoMatrix 8x8 [part_number=1487]

nets:
  N1: M2.pin_12, IC2.pin14, Part3.VDD
  N2: M2.pin_13, M2.pin_18
  N3: M2.pin_14, M2.pin_19, IC2.pin1, IC2.pin7, Part3.GND
  N4: M2.pin_20, IC2.pin2
  N5: IC2.pin3, Part3.IN

notes:
  The solder pad on the bottom of the Arduino Nano 33 Iot (VUSB) must be soldered to have access to 5V. We need this to drive the LEDs.
  Be careful not to connect this to any of the input pins, because the Arduino can only tolerate 3.3V.

custom parts:
  Arduino Nano 33 IOT-tht: The Arduino Nano 33 IoT is the easiest and cheapest point of entry to enhance existing devices (and creating new ones) to be part of the IoT and designing pico-network applications. Whether you are looking at building a sensor network connected to your office or home router, or if you want to create a BLE device sending data to a cellphone, the Nano 33 IoT is your one-stop-solution for many of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
  NeoPixel NeoMatrix 8x8: Put on your sunglasses before wiring up this LED matrix - 64 eye-blistering RGB LEDs adorn the NeoMatrix for a blast of configurable color. Arranged in an 8x8 matrix, each pixel is individually addressable. Only one microcontroller pin is required to control all the LEDs, and you get 24 bit color for each LED.
