# Fritzing sketch vision-cube-wiring (saved by Fritzing 0.9.10b)

parts:
  Part1 = Adafruit Perma-Proto HAT [part_number="Adafruit #2314 and #2310"]
  R1 = Resistor [tolerance=±5% resistance=10k package="0402 [SMD]"]
  R2 = Resistor [tolerance=±5% resistance=10k package="0402 [SMD]"]
  R3 = Resistor [tolerance=±5% resistance=10k package="0402 [SMD]"]
  R4 = Resistor [tolerance=±5% resistance=10k package="0402 [SMD]"]
  S1 = Round Pushbutton
  S2 = Round Pushbutton
  S3 = Round Pushbutton
  S4 = Round Pushbutton

nets:
  N1: Part1.GPIO4, Part1.N$50#319
  N2: Part1.GPIO22, Part1.N$46#299
  N3: Part1.GPIO25, Part1.N$43#284
  N4: Part1.GPIO12, Part1.N$39#269
  N5: Part1.3.3V, R1.Pin_0, R2.Pin_0, R3.Pin_0, R4.Pin_0
  N6: Part1.GND, Part1.N$41#274, Part1.N$44#289, Part1.N$47#304, Part1.N$49#314
  N7: Part1.N$39#268, R1.Pin_1
  N8: Part1.N$39#270, S4.leg0
  N9: Part1.N$41#275, S4.leg1
  N10: Part1.N$43#283, R2.Pin_1
  N11: Part1.N$43#285, S3.leg0
  N12: Part1.N$44#290, S3.leg1
  N13: Part1.N$46#298, R3.Pin_1
  N14: Part1.N$46#300, S2.leg0
  N15: Part1.N$47#305, S2.leg1
  N16: Part1.N$49#315, S1.leg1
  N17: Part1.N$50#318, R4.Pin_1
  N18: Part1.N$50#320, S1.leg0

notes:
  Buttons (from left to right):
  - Class 3
  - Class 2
  - Class 1
  - Reset

custom parts:
  Adafruit Perma-Proto HAT: To kick off the Adafruit HAT party, we have this Perma-Proto inspired plug in daughter board. It has a grid of 0.1" prototyping soldering holes for attaching chips, resistors, LED, potentiometers and more. The holes are connected underneath with traces to mimic the solderless breadboards you're familiar. There's also long power strips for +3V, +5V and Ground connections to the Pi. Near the top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
